// Logisim project RISC(V) LOGISM.circ as structural Verilog: 17 circuits, main circuit main
module main (
  output [31:0] out_1,
  output [31:0] out_2,
  output [31:0] out_3,
  output [31:0] out_4,
  output [31:0] out_5,
  output [31:0] out_6,
  output [31:0] out_7,
  output [1:0] out_8,
  output [31:0] out_9,
  output [31:0] out_10,
  output [1:0] out_11,
  output [31:0] out_12,
  output [31:0] out_13,
  output [3:0] out_14,
  output out_15,
  output [31:0] out_16,
  output [1:0] out_17,
  output [31:0] out_18,
  output [31:0] out_19,
  output [31:0] out_20,
  output [31:0] out_21
);

  wire branch_1_branch_out, clock_1_out, control_1_branch, control_1_mem_2_reg, control_1_reg_write,
       control_1_store, reset_out;
  wire [2:0] rom_1_data_2;
  wire [31:0] adder_1_out, imm_gen_1_out_4, imm_gen_1_out_5, imm_gen_1_out_6, imm_gen_1_out_7,
       multiplexer_4_out, multiplexer_5_out, ram_1_data, register_1_q, rom_1_data;

  Multiplexer #(.select(2), .width(32), .enable("false")) multiplexer_1 (
    .in0(adder_1_out), .in1(imm_gen_1_out_6), .in2(out_2), .in3(out_3), .out(out_6), .sel(out_8));
  Clock clock_1 (.out(clock_1_out));
  Button reset (.out(reset_out));
  Imm_Gen imm_gen_1 (
    .in_1({rom_1_data[31:15], rom_1_data_2, rom_1_data[11:0]}), .in_2(register_1_q), .out_3(out_19),
    .out_4(imm_gen_1_out_4), .out_5(imm_gen_1_out_5), .out_6(imm_gen_1_out_6), .out_7(imm_gen_1_out_7));
  Register #(.width(32)) register_1 (.D(out_6), .Q(register_1_q), .clk(clock_1_out), .clr(reset_out));  // open: en
  Adder #(.width(32)) adder_1 (.a(register_1_q), .b(32'h4), .out(adder_1_out));  // open: cin, cout
  Multiplexer #(.select(2), .width(32), .enable("false")) multiplexer_2 (
    .in0(out_19), .in1(imm_gen_1_out_4), .in2(imm_gen_1_out_7), .out(out_18), .sel(out_17));  // open: in3
  Multiplexer #(.width(32), .enable("false")) multiplexer_3 (
    .in0(adder_1_out), .in1(imm_gen_1_out_5), .out(out_3), .sel(branch_1_branch_out));
  Branch branch_1 (
    .RS_1(out_20), .RS_2(out_13), .Branch_out(branch_1_branch_out), .Selector(rom_1_data_2),
    .in_2(control_1_branch));
  ROM #(.addrWidth(12), .dataWidth(32)) rom_1 (
    .addr(register_1_q[13:2]), .data({rom_1_data[31:15], rom_1_data_2, rom_1_data[11:0]}));  // open: sel
  Register_File register_file_1 (
    .EN(control_1_reg_write), .rd(rom_1_data[11:7]), .rs1_5_bit(rom_1_data[19:15]),
    .rs2_in(rom_1_data[24:20]), .in_1(out_12), .in_6(clock_1_out), .rs2(out_13), .rs1(out_20), .x5(out_1),
    .x6(out_4), .x7(out_5), .x8(out_7), .x9(out_9), .x10(out_10));
  Multiplexer #(.width(32), .enable("false")) multiplexer_4 (
    .in0(out_18), .in1(out_13), .out(multiplexer_4_out), .sel(out_15));
  Adder #(.width(32)) adder_2 (.a(out_19), .b(out_20), .out(out_2));  // open: cin, cout
  Control control_1 (
    .opcode_7_bit(rom_1_data[6:0]), .reg_write(control_1_reg_write), .branch(control_1_branch),
    .store(control_1_store), .mem_2_reg(control_1_mem_2_reg), .op_a_selector(out_11), .op_b_selector(out_15),
    .imm_selector(out_17), .next_pc(out_8), .Func_3(rom_1_data_2), .Func_7(rom_1_data[30]), .Selector(out_14));  // open: ALU
  Multiplexer #(.select(2), .width(32), .enable("false")) multiplexer_5 (
    .in0(out_20), .in1(register_1_q), .in2(adder_1_out), .in3({32{1'b0}}), .out(multiplexer_5_out),
    .sel(out_11));
  ALU_MAIN alu_main_1 (.Selector(out_14), .Output(out_16), .RS_1(multiplexer_5_out), .RS_2(multiplexer_4_out));
  RAM #(.addrWidth(12), .dataWidth(32), .bus("separate")) ram_1 (
    .addr(out_16[13:2]), .din(out_13), .data(ram_1_data), .str(control_1_store), .clk(clock_1_out),
    .ld(control_1_mem_2_reg), .clr(reset_out));  // open: sel
  Multiplexer #(.width(32), .enable("false")) multiplexer_6 (
    .in0(out_16), .in1(ram_1_data), .out(out_12), .sel(control_1_mem_2_reg));

  assign out_21 = out_18;

  // Other names for the same wires on the sheet: _5[31:0] = out_1; _6[31:0] = out_4; _7[31:0] = out_5;
  //   _8[31:0] = out_7; _9[31:0] = out_9; _10[31:0] = out_10

  // Notes on the sheet:
  //   contents of rom_1 (hex, n*v repeats v):
  //   500293 500333 405003b3 507433 5064b3 504533 72f593 72e613 72c693
endmodule

module Type_decode (
  input  [6:0] in_1,
  output R_TYPE,
  output I_TYPE,
  output I_TYPE_LOAD,
  output JALR,
  output S_TYPE,
  output SB_TYPE,
  output AUIPC,
  output LUI_TYPE,
  output UJ_TYPE_JAL
);

  Comparator #(.width(7)) comparator_1 (.a(in_1), .b(7'b0110011), .eq(R_TYPE));  // open: gt, lt
  Comparator #(.width(7)) comparator_2 (.a(in_1), .b(7'b0010011), .eq(I_TYPE));  // open: gt, lt
  Comparator #(.width(7)) comparator_3 (.a(in_1), .b(7'b0000011), .eq(I_TYPE_LOAD));  // open: gt, lt
  Comparator #(.width(7)) comparator_4 (.a(in_1), .b(7'b1100111), .eq(JALR));  // open: gt, lt
  Comparator #(.width(7)) comparator_5 (.a(in_1), .b(7'b0100011), .eq(S_TYPE));  // open: gt, lt
  Comparator #(.width(7)) comparator_6 (.a(in_1), .b(7'b1100011), .eq(SB_TYPE));  // open: gt, lt
  Comparator #(.width(7)) comparator_7 (.a(in_1), .b(7'b0010111), .eq(AUIPC));  // open: gt, lt
  Comparator #(.width(7)) comparator_8 (.a(in_1), .b(7'b0110111), .eq(LUI_TYPE));  // open: gt, lt
  Comparator #(.width(7)) comparator_9 (.a(in_1), .b(7'b1101111), .eq(UJ_TYPE_JAL));  // open: gt, lt
endmodule

module Imm_Gen (
  input  [31:0] in_1,
  input  [31:0] in_2,
  output [31:0] out_3,
  output [31:0] out_4,
  output [31:0] out_5,
  output [31:0] out_6,
  output [31:0] out_7
);

  wire [19:0] shifter_1_out;
  wire [31:0] bit_extender_2_out, bit_extender_3_out;

  assign out_3 = {{20{in_1[31]}}, in_1[31:20]};  // Bit_Extender bit_extender_1
  assign bit_extender_2_out = {{19{in_1[31]}}, {in_1[31], in_1[7], in_1[30:25], in_1[11:8], 1'b0}};  // Bit_Extender bit_extender_2
  assign bit_extender_3_out = {{11{in_1[31]}}, {in_1[31], in_1[19:12], in_1[20], in_1[30:21], 1'b0}};  // Bit_Extender bit_extender_3
  Shifter #(.width(20)) shifter_1 (.in(in_1[31:12]), .\dist (5'b01100), .out(shifter_1_out));
  assign out_7 = {{12{shifter_1_out[19]}}, shifter_1_out};  // Bit_Extender bit_extender_4
  assign out_4 = {{20{in_1[31]}}, {in_1[31:25], in_1[11:7]}};  // Bit_Extender bit_extender_5
  Adder #(.width(32)) adder_1 (.a(bit_extender_2_out), .b(in_2), .out(out_5));  // open: cin, cout
  Adder #(.width(32)) adder_2 (.a(bit_extender_3_out), .b(in_2), .out(out_6));  // open: cin, cout

  // Notes on the sheet:
  //   INS
  //   PC     (Program Counter)
endmodule

module Register_File (
  input  [31:0] in_1,
  input  EN,
  input  [4:0] rs1_5_bit,
  input  [4:0] rd,
  input  [4:0] rs2_in,
  input  in_6,
  output [31:0] x5,
  output [31:0] x6,
  output [31:0] x7,
  output [31:0] rs1,
  output [31:0] x8,
  output [31:0] x9,
  output [31:0] x10,
  output [31:0] rs2
);

  wire decoder_1_out1, decoder_1_out2, decoder_1_out3, decoder_1_out4, decoder_1_out5, decoder_1_out6,
       decoder_1_out7, decoder_1_out8, decoder_1_out9, decoder_1_out10, decoder_1_out11, decoder_1_out12,
       decoder_1_out13, decoder_1_out14, decoder_1_out15, decoder_1_out16, decoder_1_out17, decoder_1_out18,
       decoder_1_out19, decoder_1_out20, decoder_1_out21, decoder_1_out22, decoder_1_out23, decoder_1_out24,
       decoder_1_out25, decoder_1_out26, decoder_1_out27, decoder_1_out28, decoder_1_out29, decoder_1_out30,
       decoder_1_out31;
  wire [31:0] register_1_q, register_2_q, register_3_q, register_4_q, register_11_q, register_12_q,
       register_13_q, register_14_q, register_15_q, register_16_q, register_17_q, register_18_q,
       register_19_q, register_20_q, register_21_q, register_22_q, register_23_q, register_24_q,
       register_25_q, register_26_q, register_27_q, register_28_q, register_29_q, register_30_q,
       register_31_q;

  Decoder #(.select(5), .disabled(0)) decoder_1 (
    .out1(decoder_1_out1), .out2(decoder_1_out2), .out3(decoder_1_out3), .out4(decoder_1_out4),
    .out5(decoder_1_out5), .out6(decoder_1_out6), .out7(decoder_1_out7), .out8(decoder_1_out8),
    .out9(decoder_1_out9), .out10(decoder_1_out10), .out11(decoder_1_out11), .out12(decoder_1_out12),
    .out13(decoder_1_out13), .out14(decoder_1_out14), .out15(decoder_1_out15), .out16(decoder_1_out16),
    .out17(decoder_1_out17), .out18(decoder_1_out18), .out19(decoder_1_out19), .out20(decoder_1_out20),
    .out21(decoder_1_out21), .out22(decoder_1_out22), .out23(decoder_1_out23), .out24(decoder_1_out24),
    .out25(decoder_1_out25), .out26(decoder_1_out26), .out27(decoder_1_out27), .out28(decoder_1_out28),
    .out29(decoder_1_out29), .out30(decoder_1_out30), .out31(decoder_1_out31), .sel(rd), .en(EN));  // open: out0
  Register #(.width(32)) register_1 (.D(in_1), .en(decoder_1_out1), .Q(register_1_q), .clk(in_6));  // open: clr
  Register #(.width(32)) register_2 (.D(in_1), .en(decoder_1_out2), .Q(register_2_q), .clk(in_6));  // open: clr
  Register #(.width(32)) register_3 (.D(in_1), .en(decoder_1_out3), .Q(register_3_q), .clk(in_6));  // open: clr
  Register #(.width(32)) register_4 (.D(in_1), .en(decoder_1_out4), .Q(register_4_q), .clk(in_6));  // open: clr
  Register #(.width(32)) register_5 (.D(in_1), .en(decoder_1_out5), .Q(x5), .clk(in_6));  // open: clr
  Register #(.width(32)) register_6 (.D(in_1), .en(decoder_1_out6), .Q(x6), .clk(in_6));  // open: clr
  Register #(.width(32)) register_7 (.D(in_1), .en(decoder_1_out7), .Q(x7), .clk(in_6));  // open: clr
  Register #(.width(32)) register_8 (.D(in_1), .en(decoder_1_out8), .Q(x8), .clk(in_6));  // open: clr
  Register #(.width(32)) register_9 (.D(in_1), .en(decoder_1_out9), .Q(x9), .clk(in_6));  // open: clr
  Register #(.width(32)) register_10 (.D(in_1), .en(decoder_1_out10), .Q(x10), .clk(in_6));  // open: clr
  Register #(.width(32)) register_11 (.D(in_1), .en(decoder_1_out11), .Q(register_11_q), .clk(in_6));  // open: clr
  Register #(.width(32)) register_12 (.D(in_1), .en(decoder_1_out12), .Q(register_12_q), .clk(in_6));  // open: clr
  Register #(.width(32)) register_13 (.D(in_1), .en(decoder_1_out13), .Q(register_13_q), .clk(in_6));  // open: clr
  Register #(.width(32)) register_14 (.D(in_1), .en(decoder_1_out14), .Q(register_14_q), .clk(in_6));  // open: clr
  Register #(.width(32)) register_15 (.D(in_1), .en(decoder_1_out15), .Q(register_15_q), .clk(in_6));  // open: clr
  Register #(.width(32)) register_16 (.D(in_1), .en(decoder_1_out16), .Q(register_16_q), .clk(in_6));  // open: clr
  Register #(.width(32)) register_17 (.D(in_1), .en(decoder_1_out17), .Q(register_17_q), .clk(in_6));  // open: clr
  Register #(.width(32)) register_18 (.D(in_1), .en(decoder_1_out18), .Q(register_18_q), .clk(in_6));  // open: clr
  Register #(.width(32)) register_19 (.D(in_1), .en(decoder_1_out19), .Q(register_19_q), .clk(in_6));  // open: clr
  Register #(.width(32)) register_20 (.D(in_1), .en(decoder_1_out20), .Q(register_20_q), .clk(in_6));  // open: clr
  Register #(.width(32)) register_21 (.D(in_1), .en(decoder_1_out21), .Q(register_21_q), .clk(in_6));  // open: clr
  Register #(.width(32)) register_22 (.D(in_1), .en(decoder_1_out22), .Q(register_22_q), .clk(in_6));  // open: clr
  Register #(.width(32)) register_23 (.D(in_1), .en(decoder_1_out23), .Q(register_23_q), .clk(in_6));  // open: clr
  Register #(.width(32)) register_24 (.D(in_1), .en(decoder_1_out24), .Q(register_24_q), .clk(in_6));  // open: clr
  Register #(.width(32)) register_25 (.D(in_1), .en(decoder_1_out25), .Q(register_25_q), .clk(in_6));  // open: clr
  Register #(.width(32)) register_26 (.D(in_1), .en(decoder_1_out26), .Q(register_26_q), .clk(in_6));  // open: clr
  Register #(.width(32)) register_27 (.D(in_1), .en(decoder_1_out27), .Q(register_27_q), .clk(in_6));  // open: clr
  Register #(.width(32)) register_28 (.D(in_1), .en(decoder_1_out28), .Q(register_28_q), .clk(in_6));  // open: clr
  Register #(.width(32)) register_29 (.D(in_1), .en(decoder_1_out29), .Q(register_29_q), .clk(in_6));  // open: clr
  Register #(.width(32)) register_30 (.D(in_1), .en(decoder_1_out30), .Q(register_30_q), .clk(in_6));  // open: clr
  Register #(.width(32)) register_31 (.D(in_1), .en(decoder_1_out31), .Q(register_31_q), .clk(in_6));  // open: clr
  Multiplexer #(.select(5), .width(32), .disabled(0), .enable("false")) multiplexer_1 (
    .in0({32{1'b0}}), .in1(register_1_q), .in2(register_2_q), .in3(register_3_q), .in4(register_4_q),
    .in5(x5), .in6(x6), .in7(x7), .in8(x8), .in9(x9), .in10(x10), .in11(register_11_q), .in12(register_12_q),
    .in13(register_13_q), .in14(register_14_q), .in15(register_15_q), .in16(register_16_q),
    .in17(register_17_q), .in18(register_18_q), .in19(register_19_q), .in20(register_20_q),
    .in21(register_21_q), .in22(register_22_q), .in23(register_23_q), .in24(register_24_q),
    .in25(register_25_q), .in26(register_26_q), .in27(register_27_q), .in28(register_28_q),
    .in29(register_29_q), .in30(register_30_q), .in31(register_31_q), .out(rs1), .sel(rs1_5_bit));
  Multiplexer #(.select(5), .width(32), .disabled(0), .enable("false")) multiplexer_2 (
    .in0({32{1'b0}}), .in1(register_1_q), .in2(register_2_q), .in3(register_3_q), .in4(register_4_q),
    .in5(x5), .in6(x6), .in7(x7), .in8(x8), .in9(x9), .in10(x10), .in11(register_11_q), .in12(register_12_q),
    .in13(register_13_q), .in14(register_14_q), .in15(register_15_q), .in16(register_16_q),
    .in17(register_17_q), .in18(register_18_q), .in19(register_19_q), .in20(register_20_q),
    .in21(register_21_q), .in22(register_22_q), .in23(register_23_q), .in24(register_24_q),
    .in25(register_25_q), .in26(register_26_q), .in27(register_27_q), .in28(register_28_q),
    .in29(register_29_q), .in30(register_30_q), .in31(register_31_q), .out(rs2), .sel(rs2_in));

  // Notes on the sheet:
  //   Data In
  //   RS1 OUT
  //   RS2 OUT
endmodule

module control_decode (
  input  R_Type,
  input  I_Type,
  input  Load,
  input  JALR,
  input  Store,
  input  Branch,
  input  Auipc,
  input  Lui,
  input  JAL,
  input  [2:0] func_3,
  input  fun_7,
  output REG_Write,
  output Branch_2,
  output Store_2,
  output Mem_2_Reg,
  output [1:0] Operand_A,
  output Operand_B,
  output [1:0] IMM_SELECTOR,
  output [1:0] NEXT_PC,
  output [2:0] ALU,
  output [3:0] out_21
);

  wire or_1_out, or_2_out, or_3_out, or_4_out, or_5_out;

  or or_1 (or_1_out, JALR, Load, I_Type);
  or or_2 (or_2_out, Load, I_Type);
  or or_3 (or_3_out, R_Type, or_2_out, Store, Branch);
  or or_4 (or_4_out, Auipc, Lui);
  or or_5 (or_5_out, JAL, JALR);
  or or_6 (REG_Write, I_Type, Load, JALR, R_Type, Auipc, Lui, JAL);
  operand_A_select operand_a_select_1 (
    .JAL_JALR(or_3_out), .AUIPC(Auipc), .ZERO(or_5_out), .RS1(1'b0), .output_0(Operand_A[1]),
    .output_1(Operand_A[0]));
  or or_7 (Operand_B, R_Type, Branch, Store);
  Imm imm_1 (.STYPE(Store), .UTYPE(or_4_out), .I_Type(or_1_out), .a(IMM_SELECTOR[1]), .b(IMM_SELECTOR[0]));
  PC_select pc_select_1 (.SB_TYPE(Branch), .JALR(JALR), .JAL(JAL), .a(NEXT_PC[1]), .b(NEXT_PC[0]));
  decoder decoder_1 (
    .R_Type(R_Type), .I_Type(I_Type), .Load(Load), .jalr(JALR), .Store(Store), .AUIPC(Auipc), .LUI(Lui),
    .JAL(JAL), .A(ALU[2]), .B(ALU[1]), .C(ALU[0]));
  Alu_Controller_cc alu_controller_cc_1 (
    .opcode_2(ALU[2]), .opcode_1(ALU[1]), .opcode_0(ALU[0]), .func7(fun_7), .func3_2(func_3[2]),
    .func3_1(func_3[1]), .func3_0(func_3[0]), .output_0(out_21[3]), .output_1(out_21[2]),
    .output_2(out_21[1]), .output_3(out_21[0]));

  assign Branch_2 = Branch;
  assign Mem_2_Reg = Load;
  assign Store_2 = Store;
endmodule

module operand_A_select (
  input  JAL_JALR,
  input  AUIPC,
  input  ZERO,
  input  RS1,
  output output_0,
  output output_1
);

  wire not_1_out, not_2_out, not_3_out, not_4_out;

  not not_1 (not_1_out, JAL_JALR);
  and and_1 (output_0, not_1_out, not_2_out);
  not not_2 (not_2_out, AUIPC);
  not not_3 (not_3_out, JAL_JALR);
  and and_2 (output_1, not_3_out, not_4_out);
  not not_4 (not_4_out, ZERO);
endmodule

module Imm (
  input  STYPE,
  input  UTYPE,
  input  I_Type,
  output a,
  output b
);

  wire not_1_out, not_2_out, not_3_out, not_4_out;

  not not_1 (not_1_out, STYPE);
  not not_2 (not_2_out, I_Type);
  not not_3 (not_3_out, UTYPE);
  not not_4 (not_4_out, I_Type);
  and and_1 (a, not_1_out, not_2_out);
  and and_2 (b, not_3_out, not_4_out);
endmodule

module PC_select (
  input  SB_TYPE,
  input  JALR,
  input  JAL,
  output a,
  output b
);

  or or_1 (a, JALR, SB_TYPE);
  or or_2 (b, JAL, SB_TYPE);
endmodule

module decoder (
  input  R_Type,
  input  I_Type,
  input  Load,
  input  jalr,
  input  Store,
  input  AUIPC,
  input  LUI,
  input  JAL,
  output A,
  output B,
  output C
);

  wire or_1_out, or_2_out, or_3_out, or_4_out, or_5_out, or_6_out;

  or or_1 (or_1_out, JAL, LUI);
  or or_2 (or_2_out, AUIPC, Store);
  or or_3 (or_3_out, JAL, LUI);
  or or_4 (or_4_out, jalr, Load);
  or or_5 (or_5_out, JAL, AUIPC);
  or or_6 (or_6_out, jalr, I_Type);
  or or_7 (A, or_1_out, or_2_out);
  or or_8 (B, or_3_out, or_4_out);
  or or_9 (C, or_5_out, or_6_out);
endmodule

module ALU_MAIN (
  input  [31:0] RS_1,
  input  [31:0] RS_2,
  input  [3:0] Selector,
  output [31:0] Output
);

  wire comparator_1_lt, comparator_2_lt;
  wire [31:0] adder_1_out, and_1_out, bit_extender_1_out, bit_extender_2_out, or_1_out, shifter_1_out,
       shifter_2_out, shifter_3_out, subtractor_1_out, xor_1_out;

  Adder #(.width(32)) adder_1 (.a(RS_1), .b(RS_2), .out(adder_1_out));  // open: cin, cout
  Subtractor #(.width(32)) subtractor_1 (.a(RS_1), .b(RS_2), .out(subtractor_1_out));  // open: bin, bout
  assign and_1_out = RS_1 & RS_2;  // AND_Gate and_1, 32 bits wide
  assign or_1_out = RS_1 | RS_2;  // OR_Gate or_1, 32 bits wide
  assign xor_1_out = RS_1 ^ RS_2;  // XOR_Gate xor_1, 32 bits wide
  Shifter #(.width(32)) shifter_1 (.in(RS_1), .\dist (RS_2[4:0]), .out(shifter_1_out));
  Shifter #(.width(32), .shift("lr")) shifter_2 (.in(RS_1), .\dist (RS_2[4:0]), .out(shifter_2_out));
  Shifter #(.width(32), .shift("ar")) shifter_3 (.in(RS_1), .\dist (RS_2[4:0]), .out(shifter_3_out));
  Comparator #(.width(32)) comparator_1 (.a(RS_1), .b(RS_2), .lt(comparator_1_lt));  // open: gt, eq
  Comparator #(.width(32), .mode("unsigned")) comparator_2 (.a(RS_1), .b(RS_2), .lt(comparator_2_lt));  // open: gt, eq
  assign bit_extender_1_out = {{31{1'b0}}, comparator_1_lt};  // Bit_Extender bit_extender_1
  assign bit_extender_2_out = {{31{1'b0}}, comparator_2_lt};  // Bit_Extender bit_extender_2
  Multiplexer #(.select(4), .width(32)) multiplexer_1 (
    .in0(adder_1_out), .in1(subtractor_1_out), .in2(and_1_out), .in3(or_1_out), .in4(xor_1_out),
    .in5(shifter_1_out), .in6(shifter_2_out), .in7(bit_extender_1_out), .in8(bit_extender_2_out),
    .in9(shifter_3_out), .in15(RS_2), .out(Output), .sel(Selector));  // open: in10, in11, in12, in13, in14, en
endmodule

module Alu_Controller (
  input  opcode_0,
  input  opcode_1,
  input  opcode_2,
  input  func_3_0,
  input  func_3_1,
  input  func_3_2,
  input  func_7,
  output output_0,
  output output_1,
  output output_2,
  output output_3
);

  wire and_1_out, and_2_out, and_3_out, and_4_out, and_5_out, and_6_out, and_7_out, and_8_out, and_9_out,
       and_10_out, and_11_out, and_12_out, and_13_out, and_14_out, and_15_out, and_16_out, not_1_out,
       not_2_out, not_3_out, not_4_out, not_5_out, not_6_out, not_7_out, not_8_out, not_9_out, not_10_out,
       not_11_out, not_12_out, not_13_out, not_14_out, not_15_out, not_16_out, not_17_out, not_18_out,
       not_19_out, not_20_out, not_21_out, not_22_out, not_23_out, not_24_out, not_25_out, not_26_out,
       not_27_out, not_28_out, not_29_out, not_30_out, not_31_out;

  not not_1 (not_1_out, opcode_0);
  not not_2 (not_2_out, func_3_1);
  not not_3 (not_3_out, opcode_0);
  not not_4 (not_4_out, func_3_2);
  not not_5 (not_5_out, opcode_0);
  not not_6 (not_6_out, func_3_0);
  not not_7 (not_7_out, func_3_2);
  not not_8 (not_8_out, opcode_0);
  not not_9 (not_9_out, opcode_2);
  not not_10 (not_10_out, func_3_1);
  not not_11 (not_11_out, func_7);
  not not_12 (not_12_out, opcode_0);
  not not_13 (not_13_out, func_3_2);
  not not_14 (not_14_out, func_7);
  not not_15 (not_15_out, opcode_0);
  not not_16 (not_16_out, opcode_2);
  not not_17 (not_17_out, func_7);
  not not_18 (not_18_out, opcode_0);
  not not_19 (not_19_out, func_3_0);
  not not_20 (not_20_out, opcode_0);
  not not_21 (not_21_out, opcode_0);
  not not_22 (not_22_out, func_3_1);
  not not_23 (not_23_out, func_3_2);
  not not_24 (not_24_out, opcode_0);
  not not_25 (not_25_out, opcode_2);
  not not_26 (not_26_out, func_7);
  not not_27 (not_27_out, opcode_1);
  not not_28 (not_28_out, opcode_2);
  not not_29 (not_29_out, func_3_2);
  not not_30 (not_30_out, opcode_0);
  not not_31 (not_31_out, func_3_2);
  and and_1 (and_1_out, not_1_out, not_2_out, func_3_2, func_7);
  and and_2 (and_2_out, not_3_out, func_3_0, not_4_out, func_7);
  and and_3 (and_3_out, opcode_1, opcode_2);
  and and_4 (and_4_out, not_5_out, not_6_out, not_7_out, func_7);
  and and_5 (and_5_out, not_8_out, not_9_out, not_10_out, func_3_2, not_11_out);
  and and_6 (and_6_out, not_12_out, func_3_1, not_13_out, not_14_out);
  and and_7 (and_7_out, opcode_1, opcode_2);
  and and_8 (and_8_out, not_15_out, not_16_out, func_3_2, not_17_out);
  and and_9 (and_9_out, not_18_out, not_19_out, func_3_1, func_7);
  and and_10 (and_10_out, not_20_out, func_3_1, func_3_2);
  and and_11 (and_11_out, opcode_1, opcode_2);
  and and_12 (and_12_out, not_21_out, not_22_out, not_23_out, func_7);
  and and_13 (and_13_out, not_24_out, not_25_out, func_3_2, not_26_out);
  and and_14 (and_14_out, not_27_out, not_28_out, func_3_0, not_29_out);
  and and_15 (and_15_out, not_30_out, func_3_0, not_31_out, func_7);
  and and_16 (and_16_out, opcode_1, opcode_2);
  or or_1 (output_0, and_1_out, and_2_out, and_3_out);
  or or_2 (output_1, and_4_out, and_5_out, and_6_out, and_7_out);
  or or_3 (output_2, and_8_out, and_9_out, and_10_out, and_11_out);
  or or_4 (output_3, and_12_out, and_13_out, and_14_out, and_15_out, and_16_out);
endmodule

module Control (
  input  [6:0] opcode_7_bit,
  input  [2:0] Func_3,
  input  Func_7,
  output reg_write,
  output branch,
  output store,
  output mem_2_reg,
  output [1:0] op_a_selector,
  output op_b_selector,
  output [1:0] imm_selector,
  output [1:0] next_pc,
  output [2:0] ALU,
  output [3:0] Selector
);

  wire type_decode_1_auipc, type_decode_1_i_type, type_decode_1_i_type_load, type_decode_1_jalr,
       type_decode_1_lui_type, type_decode_1_r_type, type_decode_1_s_type, type_decode_1_sb_type,
       type_decode_1_uj_type_jal;

  Type_decode type_decode_1 (
    .in_1(opcode_7_bit), .R_TYPE(type_decode_1_r_type), .I_TYPE(type_decode_1_i_type),
    .I_TYPE_LOAD(type_decode_1_i_type_load), .JALR(type_decode_1_jalr), .S_TYPE(type_decode_1_s_type),
    .SB_TYPE(type_decode_1_sb_type), .AUIPC(type_decode_1_auipc), .LUI_TYPE(type_decode_1_lui_type),
    .UJ_TYPE_JAL(type_decode_1_uj_type_jal));
  control_decode control_decode_1 (
    .func_3(Func_3), .fun_7(Func_7), .REG_Write(reg_write), .Branch_2(branch), .Store_2(store),
    .Mem_2_Reg(mem_2_reg), .Operand_A(op_a_selector), .Operand_B(op_b_selector), .IMM_SELECTOR(imm_selector),
    .NEXT_PC(next_pc), .ALU(ALU), .R_Type(type_decode_1_r_type), .I_Type(type_decode_1_i_type),
    .Load(type_decode_1_i_type_load), .JALR(type_decode_1_jalr), .Store(type_decode_1_s_type),
    .Branch(type_decode_1_sb_type), .Auipc(type_decode_1_auipc), .Lui(type_decode_1_lui_type),
    .JAL(type_decode_1_uj_type_jal), .out_21(Selector));
endmodule

module OP_select (
  input  JAL_JALR,
  input  AUIPC,
  input  ZERO,
  input  RS1,
  output output_0,
  output output_1
);

  wire and_2_out, and_3_out, and_4_out, and_5_out, not_1_out, not_2_out, not_3_out, not_4_out, not_5_out,
       not_6_out, not_7_out, not_8_out;

  not not_1 (not_1_out, JAL_JALR);
  and and_1 (output_0, not_1_out, not_2_out);
  not not_2 (not_2_out, RS1);
  not not_3 (not_3_out, JAL_JALR);
  and and_2 (and_2_out, not_3_out, not_4_out);
  not not_4 (not_4_out, AUIPC);
  not not_5 (not_5_out, RS1);
  not not_6 (not_6_out, AUIPC);
  and and_3 (and_3_out, not_6_out, not_7_out);
  not not_7 (not_7_out, ZERO);
  not not_8 (not_8_out, RS1);
  and and_4 (and_4_out, and_2_out, not_5_out);
  and and_5 (and_5_out, and_3_out, not_8_out);
  or or_1 (output_1, and_4_out, and_5_out);
endmodule

module Branch (
  input  [31:0] RS_1,
  input  in_2,
  input  [2:0] Selector,
  input  [31:0] RS_2,
  output Branch_out
);

  wire comparator_1_eq, comparator_2_eq, comparator_3_lt, comparator_4_eq, comparator_4_gt, comparator_5_lt,
       comparator_6_eq, comparator_6_gt, not_1_out, or_1_out, or_2_out;

  Comparator #(.width(32)) comparator_1 (.a(RS_1), .b(RS_2), .eq(comparator_1_eq));  // open: gt, lt
  Comparator #(.width(32)) comparator_2 (.a(RS_1), .b(RS_2), .eq(comparator_2_eq));  // open: gt, lt
  Comparator #(.width(32)) comparator_3 (.a(RS_1), .b(RS_2), .lt(comparator_3_lt));  // open: gt, eq
  Comparator #(.width(32)) comparator_4 (.a(RS_1), .b(RS_2), .gt(comparator_4_gt), .eq(comparator_4_eq));  // open: lt
  Comparator #(.width(32), .mode("unsigned")) comparator_5 (.a(RS_1), .b(RS_2), .lt(comparator_5_lt));  // open: gt, eq
  Comparator #(.width(32), .mode("unsigned")) comparator_6 (
    .a(RS_1), .b(RS_2), .gt(comparator_6_gt), .eq(comparator_6_eq));  // open: lt
  not not_1 (not_1_out, comparator_2_eq);
  or or_1 (or_1_out, comparator_4_gt, comparator_4_eq);
  or or_2 (or_2_out, comparator_6_gt, comparator_6_eq);
  Multiplexer #(.select(3)) multiplexer_1 (
    .in0(comparator_1_eq), .in1(not_1_out), .in4(comparator_3_lt), .in5(or_1_out), .in6(comparator_5_lt),
    .in7(or_2_out), .out(Branch_out), .sel(Selector), .en(in_2));  // open: in2, in3

  // Notes on the sheet:
  //         beq
  //        bne
  //   blt
  //   bge
  //    bltu
endmodule

module operand (
  input  JAL_JALR,
  input  AUIPC,
  input  ZERO,
  input  RS1,
  output output_0,
  output output_1
);

  or or_1 (output_0, ZERO, AUIPC);
  or or_2 (output_1, ZERO, JAL_JALR);
endmodule

module Alu_Controller__c (
  input  opcode_0,
  input  opcode_1,
  input  opcode_2,
  input  func_3_0,
  input  func_3_1,
  input  func_3_2,
  input  func_7,
  output output_0,
  output output_1,
  output output_2,
  output output_3
);

  wire and_1_out, and_2_out, and_3_out, and_4_out, and_5_out, and_6_out, and_7_out, and_8_out, and_9_out,
       and_10_out, and_11_out, and_12_out, and_13_out, and_14_out, and_15_out, and_16_out, and_17_out,
       and_18_out, and_19_out, and_20_out, and_21_out, and_22_out, and_23_out, and_24_out, and_25_out,
       and_26_out, and_27_out, and_28_out, and_29_out, and_30_out, and_31_out, and_32_out, and_33_out,
       and_34_out, and_35_out, and_36_out, and_37_out, and_38_out, and_39_out, and_40_out, not_1_out,
       not_2_out, not_3_out, not_4_out, not_5_out, not_6_out, not_7_out, not_8_out, not_9_out, not_10_out,
       not_11_out, not_12_out, not_13_out, not_14_out, not_15_out, not_16_out, not_17_out, not_18_out,
       not_19_out, not_20_out, not_21_out, not_22_out, not_23_out, not_24_out, not_25_out, not_26_out,
       not_27_out, not_28_out, not_29_out, not_30_out, not_31_out, or_1_out, or_2_out, or_3_out, or_4_out,
       or_6_out, or_7_out, or_9_out, or_10_out;

  not not_1 (not_1_out, opcode_0);
  not not_2 (not_2_out, func_3_1);
  not not_3 (not_3_out, opcode_0);
  not not_4 (not_4_out, func_3_2);
  not not_5 (not_5_out, opcode_0);
  not not_6 (not_6_out, opcode_2);
  not not_7 (not_7_out, opcode_0);
  not not_8 (not_8_out, opcode_2);
  not not_9 (not_9_out, func_7);
  not not_10 (not_10_out, opcode_0);
  not not_11 (not_11_out, func_3_0);
  not not_12 (not_12_out, opcode_0);
  not not_13 (not_13_out, opcode_0);
  not not_14 (not_14_out, func_3_1);
  not not_15 (not_15_out, func_3_2);
  not not_16 (not_16_out, opcode_0);
  not not_17 (not_17_out, opcode_2);
  not not_18 (not_18_out, func_7);
  and and_1 (and_1_out, not_1_out, not_2_out);
  and and_2 (and_2_out, func_3_2, func_7);
  and and_3 (and_3_out, not_3_out, func_3_0);
  and and_4 (and_4_out, not_4_out, func_7);
  not not_19 (not_19_out, opcode_0);
  not not_20 (not_20_out, func_3_0);
  not not_21 (not_21_out, func_3_2);
  and and_5 (and_5_out, not_5_out, not_6_out);
  not not_22 (not_22_out, func_3_1);
  not not_23 (not_23_out, func_7);
  not not_24 (not_24_out, opcode_0);
  not not_25 (not_25_out, func_3_2);
  not not_26 (not_26_out, func_7);
  and and_6 (and_6_out, not_7_out, not_8_out);
  and and_7 (and_7_out, func_3_2, not_9_out);
  and and_8 (and_8_out, not_10_out, not_11_out);
  and and_9 (and_9_out, func_3_1, func_7);
  and and_10 (and_10_out, not_12_out, func_3_1);
  and and_11 (and_11_out, not_13_out, not_14_out);
  and and_12 (and_12_out, not_15_out, func_7);
  and and_13 (and_13_out, not_16_out, not_17_out);
  and and_14 (and_14_out, func_3_2, not_18_out);
  not not_27 (not_27_out, opcode_1);
  not not_28 (not_28_out, opcode_2);
  not not_29 (not_29_out, func_3_2);
  not not_30 (not_30_out, opcode_0);
  not not_31 (not_31_out, func_3_2);
  and and_15 (and_15_out, and_1_out, and_2_out);
  and and_16 (and_16_out, and_3_out, and_4_out);
  and and_17 (and_17_out, not_19_out, not_20_out);
  and and_18 (and_18_out, not_21_out, func_7);
  and and_19 (and_19_out, and_5_out, not_22_out);
  and and_20 (and_20_out, func_3_2, not_23_out);
  and and_21 (and_21_out, not_24_out, func_3_1);
  and and_22 (and_22_out, not_25_out, not_26_out);
  and and_23 (and_23_out, and_6_out, and_7_out);
  and and_24 (and_24_out, and_8_out, and_9_out);
  and and_25 (and_25_out, and_10_out, func_3_2);
  and and_26 (and_26_out, opcode_1, opcode_2);
  and and_27 (and_27_out, and_11_out, and_12_out);
  and and_28 (and_28_out, and_13_out, and_14_out);
  and and_29 (and_29_out, not_27_out, not_28_out);
  and and_30 (and_30_out, func_3_0, not_29_out);
  and and_31 (and_31_out, not_30_out, func_3_0);
  and and_32 (and_32_out, not_31_out, func_7);
  or or_1 (or_1_out, and_15_out, and_16_out);
  and and_33 (and_33_out, opcode_1, opcode_2);
  and and_34 (and_34_out, and_17_out, and_18_out);
  and and_35 (and_35_out, and_19_out, and_20_out);
  and and_36 (and_36_out, and_21_out, and_22_out);
  and and_37 (and_37_out, opcode_1, opcode_2);
  or or_2 (or_2_out, and_23_out, and_24_out);
  or or_3 (or_3_out, and_25_out, and_26_out);
  or or_4 (or_4_out, and_27_out, and_28_out);
  and and_38 (and_38_out, and_29_out, and_30_out);
  and and_39 (and_39_out, and_31_out, and_32_out);
  and and_40 (and_40_out, opcode_1, opcode_2);
  or or_5 (output_0, or_1_out, and_33_out);
  or or_6 (or_6_out, and_34_out, and_35_out);
  or or_7 (or_7_out, and_36_out, and_37_out);
  or or_8 (output_2, or_2_out, or_3_out);
  or or_9 (or_9_out, or_4_out, and_38_out);
  or or_10 (or_10_out, and_39_out, and_40_out);
  or or_11 (output_1, or_6_out, or_7_out);
  or or_12 (output_3, or_9_out, or_10_out);
endmodule

module Alu_Controller_cc (
  input  opcode_2,
  input  opcode_1,
  input  opcode_0,
  input  func7,
  input  func3_2,
  input  func3_1,
  input  func3_0,
  output output_0,
  output output_1,
  output output_2,
  output output_3
);

  wire and_1_out, and_2_out, and_3_out, and_4_out, and_5_out, and_6_out, and_7_out, and_8_out, and_9_out,
       and_10_out, and_11_out, and_12_out, and_13_out, and_14_out, and_15_out, and_16_out, and_17_out,
       and_18_out, and_19_out, and_20_out, and_21_out, and_22_out, and_23_out, and_24_out, and_25_out,
       and_26_out, and_27_out, and_28_out, and_29_out, and_30_out, and_31_out, and_32_out, and_33_out,
       and_34_out, and_35_out, and_36_out, and_37_out, and_38_out, and_39_out, and_40_out, not_1_out,
       not_2_out, not_3_out, not_4_out, not_5_out, not_6_out, not_7_out, not_8_out, not_9_out, not_10_out,
       not_11_out, not_12_out, not_13_out, not_14_out, not_15_out, not_16_out, not_17_out, not_18_out,
       not_19_out, not_20_out, not_21_out, not_22_out, not_23_out, not_24_out, not_25_out, not_26_out,
       not_27_out, not_28_out, not_29_out, not_30_out, not_31_out, or_1_out, or_2_out, or_3_out, or_4_out,
       or_6_out, or_7_out, or_9_out, or_10_out;

  not not_1 (not_1_out, opcode_2);
  not not_2 (not_2_out, func3_2);
  not not_3 (not_3_out, opcode_2);
  not not_4 (not_4_out, func3_1);
  not not_5 (not_5_out, opcode_2);
  not not_6 (not_6_out, opcode_0);
  not not_7 (not_7_out, opcode_2);
  not not_8 (not_8_out, opcode_0);
  not not_9 (not_9_out, func3_0);
  not not_10 (not_10_out, opcode_2);
  not not_11 (not_11_out, func7);
  not not_12 (not_12_out, opcode_2);
  not not_13 (not_13_out, opcode_2);
  not not_14 (not_14_out, func3_2);
  not not_15 (not_15_out, func3_1);
  not not_16 (not_16_out, opcode_2);
  not not_17 (not_17_out, opcode_0);
  not not_18 (not_18_out, func3_0);
  and and_1 (and_1_out, not_1_out, not_2_out);
  and and_2 (and_2_out, func3_1, func3_0);
  and and_3 (and_3_out, not_3_out, func7);
  and and_4 (and_4_out, not_4_out, func3_0);
  not not_19 (not_19_out, opcode_2);
  not not_20 (not_20_out, func7);
  not not_21 (not_21_out, func3_1);
  and and_5 (and_5_out, not_5_out, not_6_out);
  not not_22 (not_22_out, func3_2);
  not not_23 (not_23_out, func3_0);
  not not_24 (not_24_out, opcode_2);
  not not_25 (not_25_out, func3_1);
  not not_26 (not_26_out, func3_0);
  and and_6 (and_6_out, not_7_out, not_8_out);
  and and_7 (and_7_out, func3_1, not_9_out);
  and and_8 (and_8_out, not_10_out, not_11_out);
  and and_9 (and_9_out, func3_2, func3_0);
  and and_10 (and_10_out, not_12_out, func3_2);
  and and_11 (and_11_out, not_13_out, not_14_out);
  and and_12 (and_12_out, not_15_out, func3_0);
  and and_13 (and_13_out, not_16_out, not_17_out);
  and and_14 (and_14_out, func3_1, not_18_out);
  not not_27 (not_27_out, opcode_1);
  not not_28 (not_28_out, opcode_0);
  not not_29 (not_29_out, func3_1);
  not not_30 (not_30_out, opcode_2);
  not not_31 (not_31_out, func3_1);
  and and_15 (and_15_out, and_1_out, and_2_out);
  and and_16 (and_16_out, and_3_out, and_4_out);
  and and_17 (and_17_out, not_19_out, not_20_out);
  and and_18 (and_18_out, not_21_out, func3_0);
  and and_19 (and_19_out, and_5_out, not_22_out);
  and and_20 (and_20_out, func3_1, not_23_out);
  and and_21 (and_21_out, not_24_out, func3_2);
  and and_22 (and_22_out, not_25_out, not_26_out);
  and and_23 (and_23_out, and_6_out, and_7_out);
  and and_24 (and_24_out, and_8_out, and_9_out);
  and and_25 (and_25_out, and_10_out, func3_1);
  and and_26 (and_26_out, opcode_1, opcode_0);
  and and_27 (and_27_out, and_11_out, and_12_out);
  and and_28 (and_28_out, and_13_out, and_14_out);
  and and_29 (and_29_out, not_27_out, not_28_out);
  and and_30 (and_30_out, func7, not_29_out);
  and and_31 (and_31_out, not_30_out, func7);
  and and_32 (and_32_out, not_31_out, func3_0);
  or or_1 (or_1_out, and_15_out, and_16_out);
  and and_33 (and_33_out, opcode_1, opcode_0);
  and and_34 (and_34_out, and_17_out, and_18_out);
  and and_35 (and_35_out, and_19_out, and_20_out);
  and and_36 (and_36_out, and_21_out, and_22_out);
  and and_37 (and_37_out, opcode_1, opcode_0);
  or or_2 (or_2_out, and_23_out, and_24_out);
  or or_3 (or_3_out, and_25_out, and_26_out);
  or or_4 (or_4_out, and_27_out, and_28_out);
  and and_38 (and_38_out, and_29_out, and_30_out);
  and and_39 (and_39_out, and_31_out, and_32_out);
  and and_40 (and_40_out, opcode_1, opcode_0);
  or or_5 (output_0, or_1_out, and_33_out);
  or or_6 (or_6_out, and_34_out, and_35_out);
  or or_7 (or_7_out, and_36_out, and_37_out);
  or or_8 (output_2, or_2_out, or_3_out);
  or or_9 (or_9_out, or_4_out, and_38_out);
  or or_10 (or_10_out, and_39_out, and_40_out);
  or or_11 (output_1, or_6_out, or_7_out);
  or or_12 (output_3, or_9_out, or_10_out);
endmodule
